// Digital circuit decoder.dig as structural Verilog
module decoder (
  input  prog,
  input  [31:0] bypass,
  input  [31:0] instruction,
  output [15:0] A,
  output [1:0] rs,
  output [1:0] rd,
  output add,
  output jump
);

  wire [31:18] multiplexer_1_out;

  Multiplexer #(.Bits(32)) multiplexer_1 (
    .sel(prog), .in_0(instruction), .in_1(bypass),
    .out({multiplexer_1_out[31:22], rs, multiplexer_1_out[19:18], rd, A}));
  Decoder #(.Selector_Bits(3)) decoder_1 (
    .sel(multiplexer_1_out[26:24]), .out_0(add), .out_7(jump));  // open: out_1, out_2, out_3, out_4, out_5, out_6
endmodule
