// Digital circuit execute.dig as structural Verilog
module execute (
  input  [15:0] L,
  input  [15:0] R,
  input  add,
  output [15:0] result
);

  wire [15:0] Add_s;

  Add #(.Bits(16)) u_Add (.a(L), .b(R), .c_i(1'b0), .s(Add_s));  // open: c_o
  Multiplexer #(.Bits(16)) multiplexer_1 (.sel(add), .in_0(R), .in_1(Add_s), .out(result));

  // Notes on the sheet:
  //   L: default 1
  //   R: default 2
endmodule
